# Fritzing sketch schematic (saved by Fritzing 0.9.0b)
breadboards: 1

parts:
  LCD1 = LCD screen
  U1 = POT [package=alps_pot]
  S1 = Pushbutton [package="[THT]"]
  S2 = Pushbutton [package="[THT]"]
  S3 = Pushbutton [package="[THT]"]
  Componente2 = Arduino Uno (Rev3)
  R1 = Resistor [tolerance=±5% resistance=330 package=THT]
  R2 = Resistor [tolerance=±5% resistance=330 package=THT]
  R3 = Resistor [tolerance=±5% resistance=330 package=THT]

nets:
  VSS: LCD1.VSS, LCD1.R/W, LCD1.LED-, U1.E, Componente2.GND, R1.Pin_1, R2.Pin_1, R3.Pin_1
  VDD: LCD1.VDD, LCD1.LED+, U1.A, S1.Pin_1, S1.Pin_2, S2.Pin_1, S2.Pin_2, S3.Pin_1, S3.Pin_2, Componente2.5V
  N1: LCD1.V0, U1.S
  N2: LCD1.RS, Componente2.D12/MISO
  N3: LCD1.E, Componente2.D11_PWM/MOSI
  N4: LCD1.DB4, Componente2.D5_PWM
  N5: LCD1.DB5, Componente2.D4
  N6: LCD1.DB6, Componente2.D3_PWM
  N7: LCD1.DB7, Componente2.D2
  N8: S1.Pin_3, S1.Pin_4, Componente2.D10_PWM/SS, R1.Pin_0
  N9: S2.Pin_3, S2.Pin_4, Componente2.D9_PWM, R2.Pin_0
  N10: S3.Pin_3, S3.Pin_4, Componente2.D8, R3.Pin_0
